// Logisim project CS301Project3 .circ as structural Verilog: 14 circuits, main circuit NewMain
module Processor (
  input  [31:0] DataFromBus,
  output [15:0] Addr,
  output MemWriteEnable,
  output [31:0] Data,
  output AddrBusWrite,
  output DatabusWrite,
  output ControlBusWrite
);

  wire and_1_out, and_2_out, and_3_out, bit_extender_1_out, control_1_beq, control_1_bne,
       control_1_jalsignal, control_1_memtoreg, control_1_we_reg, not_1_out, or_1_out, or_3_out;
  wire [0:0] control_1_pcsrc;
  wire [1:0] control_1_toalu_signal, or_2_out;
  wire [2:0] control_1_alu_signal;
  wire [4:0] control_1_ins11_15, control_1_ins16_20, control_1_ins21_25, control_1_sa;
  wire [15:0] adder_1_out, adder_2_out, bit_extender_5_out, control_1_imm0_15, multiplexer_2_out, pc_1_out_2;
  wire [31:0] alu_1_alu_out, bit_extender_2_out, bit_extender_3_out, bit_extender_4_out, insmem_1_out_2,
       multiplexer_1_out, multiplexer_3_out, multiplexer_4_out, multiplexer_5_out, registerfile_1_rs_data;

  PC pc_1 (.in_1(multiplexer_2_out), .out_2(pc_1_out_2));
  Adder #(.width(16)) adder_1 (.a(16'h1), .b(pc_1_out_2), .out(adder_1_out));  // open: cin, cout
  InsMem insmem_1 (.in_1(pc_1_out_2), .out_2(insmem_1_out_2));
  Control control_1 (
    .jalsignal(control_1_jalsignal), .MemtoReg(control_1_memtoreg), .RegtoMem(DatabusWrite),
    .toALU_Signal(control_1_toalu_signal), .ALU_Signal(control_1_alu_signal),
    .PCsrc({or_2_out[1], control_1_pcsrc[0]}), .ins21_25(control_1_ins21_25), .bne(control_1_bne),
    .beq(control_1_beq), .sa(control_1_sa), .Imm0_15(control_1_imm0_15), .ins16_20(control_1_ins16_20),
    .we_reg(control_1_we_reg), .ins11_15(control_1_ins11_15), .Instruction(insmem_1_out_2));
  Bit_Extender #(.in_width(32), .out_width(1), .\type ("zero")) bit_extender_1 (
    .in(alu_1_alu_out), .out(bit_extender_1_out));
  assign bit_extender_2_out = {{16{1'b0}}, adder_1_out};  // Bit_Extender bit_extender_2
  and and_1 (and_1_out, control_1_bne, not_1_out);
  not not_1 (not_1_out, bit_extender_1_out);
  and and_2 (and_2_out, control_1_beq, bit_extender_1_out);
  or or_1 (or_1_out, and_1_out, and_2_out);
  // Probe on control_1_imm0_15
  Adder #(.width(16)) adder_2 (.a(pc_1_out_2), .b(control_1_imm0_15), .out(adder_2_out));  // open: cin, cout
  and and_3 (and_3_out, control_1_pcsrc[0], or_2_out[1]);
  // Probe on adder_2_out
  or or_2 (or_2_out[0], or_1_out, and_3_out);
  // Probe on multiplexer_1_out
  Multiplexer #(.enable("false"), .width(32)) multiplexer_1 (
    .in0(multiplexer_5_out), .in1(bit_extender_2_out), .out(multiplexer_1_out), .sel(control_1_jalsignal));
  // Probe on or_2_out
  assign bit_extender_3_out = {{27{1'b0}}, control_1_sa};  // Bit_Extender bit_extender_3
  assign bit_extender_4_out = {{16{control_1_imm0_15[15]}}, control_1_imm0_15};  // Bit_Extender bit_extender_4
  // Probe on multiplexer_3_out
  Bit_Extender #(.in_width(32), .\type ("zero")) bit_extender_5 (.in(Data), .out(bit_extender_5_out));
  RegisterFile registerfile_1 (
    .rs_data(registerfile_1_rs_data), .rt_data(Data), .we_reg(control_1_we_reg),
    .reg_towrite(control_1_ins11_15), .rtselect(control_1_ins16_20), .rsselect(control_1_ins21_25),
    .write_data(multiplexer_1_out));
  Multiplexer #(.enable("false"), .select(2), .width(16)) multiplexer_2 (
    .in0(adder_1_out), .in1(adder_2_out), .in2(control_1_imm0_15), .in3(bit_extender_5_out),
    .out(multiplexer_2_out), .sel(or_2_out));
  Multiplexer #(.enable("false"), .select(2), .width(32)) multiplexer_3 (
    .in0(registerfile_1_rs_data), .in1(bit_extender_4_out), .in2(bit_extender_3_out),
    .out(multiplexer_3_out), .sel(control_1_toalu_signal));  // open: in3
  // Probe on Data
  Multiplexer #(.enable("false"), .width(32)) multiplexer_4 (
    .in0(alu_1_alu_out), .in1(bit_extender_4_out), .out(multiplexer_4_out), .sel(or_3_out));
  ALU alu_1 (.ALU_OUT(alu_1_alu_out), .IN1(Data), .IN2(multiplexer_3_out), .ALU_Signal(control_1_alu_signal));
  or or_3 (or_3_out, control_1_memtoreg, DatabusWrite);
  Bit_Extender #(.in_width(32), .\type ("zero")) bit_extender_6 (.in(multiplexer_4_out), .out(Addr));
  or or_4 (AddrBusWrite, control_1_memtoreg, DatabusWrite);
  Multiplexer #(.enable("false"), .width(32)) multiplexer_5 (
    .in0(alu_1_alu_out), .in1(DataFromBus), .out(multiplexer_5_out), .sel(control_1_memtoreg));
  // Probe on multiplexer_5_out

  assign ControlBusWrite = AddrBusWrite;
  assign MemWriteEnable = DatabusWrite;
endmodule

module registers (
  input  [31:0] r0in,
  input  [31:0] r1in,
  input  [31:0] r2in,
  input  [31:0] r3in,
  input  r1we,
  input  r2we,
  input  r3we,
  input  [31:0] r4in,
  input  [31:0] r5in,
  input  [31:0] r6in,
  input  [31:0] r7in,
  input  r4we,
  input  r5we,
  input  r6we,
  input  r7we,
  input  [31:0] r8in,
  input  [31:0] r9in,
  input  [31:0] r10in,
  input  [31:0] r11in,
  input  r8we,
  input  in_21,
  input  in_22,
  input  in_23,
  input  [31:0] r12in,
  input  [31:0] r13in,
  input  [31:0] r14in,
  input  [31:0] r15in,
  input  in_28,
  input  in_29,
  input  in_30,
  input  in_31,
  input  [31:0] r16in,
  input  [31:0] r17in,
  input  [31:0] in_34,
  input  [31:0] in_35,
  input  in_36,
  input  in_37,
  input  in_38,
  input  in_39,
  input  [31:0] in_40,
  input  [31:0] in_41,
  input  [31:0] in_42,
  input  [31:0] in_43,
  input  in_44,
  input  in_45,
  input  in_46,
  input  in_47,
  input  [31:0] in_48,
  input  [31:0] in_49,
  input  [31:0] in_50,
  input  [31:0] in_51,
  input  in_52,
  input  in_53,
  input  in_54,
  input  in_55,
  input  [31:0] in_56,
  input  [31:0] in_57,
  input  [31:0] in_58,
  input  [31:0] r31in,
  input  in_60,
  input  in_61,
  input  in_62,
  input  r31write,
  output [31:0] r0out,
  output [31:0] r1out,
  output [31:0] r2out,
  output [31:0] r3out,
  output [31:0] r4out,
  output [31:0] r5out,
  output [31:0] r6out,
  output [31:0] r7out,
  output [31:0] out_72,
  output [31:0] out_73,
  output [31:0] out_74,
  output [31:0] out_75,
  output [31:0] out_76,
  output [31:0] out_77,
  output [31:0] out_78,
  output [31:0] out_79,
  output [31:0] out_80,
  output [31:0] out_81,
  output [31:0] out_82,
  output [31:0] out_83,
  output [31:0] out_84,
  output [31:0] out_85,
  output [31:0] out_86,
  output [31:0] out_87,
  output [31:0] out_88,
  output [31:0] out_89,
  output [31:0] out_90,
  output [31:0] out_91,
  output [31:0] out_92,
  output [31:0] out_93,
  output [31:0] out_94,
  output [31:0] r31out
);

  wire clock_1_out, clock_2_out, clock_3_out, clock_4_out, clock_5_out, clock_6_out, clock_7_out,
       clock_8_out, clock_9_out, clock_10_out, clock_11_out, clock_12_out, clock_13_out, clock_14_out,
       clock_15_out, clock_16_out, clock_17_out, clock_18_out, clock_19_out, clock_20_out, clock_21_out,
       clock_22_out, clock_23_out, clock_24_out, clock_25_out, clock_26_out, clock_27_out, clock_28_out,
       clock_29_out, clock_30_out, clock_31_out, clock_32_out;

  Register #(.width(32)) r0 (.D(r0in), .en(1'b0), .clk(clock_1_out), .Q(r0out));  // open: clr
  Clock clock_1 (.out(clock_1_out));
  Register #(.width(32)) r4 (.D(r4in), .en(r4we), .clk(clock_2_out), .Q(r4out));  // open: clr
  Clock clock_2 (.out(clock_2_out));
  Register #(.width(32)) t4 (.D(r12in), .en(in_28), .clk(clock_3_out), .Q(out_76));  // open: clr
  Clock clock_3 (.out(clock_3_out));
  Register #(.width(32)) r16 (.D(r16in), .en(in_36), .clk(clock_4_out), .Q(out_80));  // open: clr
  Clock clock_4 (.out(clock_4_out));
  Register #(.width(32)) s4 (.D(in_40), .en(in_44), .clk(clock_5_out), .Q(out_84));  // open: clr
  Clock clock_5 (.out(clock_5_out));
  Register #(.width(32)) register_1 (.D(in_48), .en(in_52), .clk(clock_6_out), .Q(out_88));  // open: clr
  Clock clock_6 (.out(clock_6_out));
  Register #(.width(32)) register_2 (.D(in_56), .en(in_60), .clk(clock_7_out), .Q(out_92));  // open: clr
  Clock clock_7 (.out(clock_7_out));
  Register #(.width(32)) r8 (.D(r8in), .en(r8we), .clk(clock_8_out), .Q(out_72));  // open: clr
  Clock clock_8 (.out(clock_8_out));
  Register #(.width(32)) r1 (.D(r1in), .en(r1we), .clk(clock_9_out), .Q(r1out));  // open: clr
  Clock clock_9 (.out(clock_9_out));
  Register #(.width(32)) r5 (.D(r5in), .en(r5we), .clk(clock_10_out), .Q(r5out));  // open: clr
  Clock clock_10 (.out(clock_10_out));
  Register #(.width(32)) t1 (.D(r9in), .en(in_21), .clk(clock_11_out), .Q(out_73));  // open: clr
  Clock clock_11 (.out(clock_11_out));
  Register #(.width(32)) register_3 (.D(r13in), .en(in_29), .clk(clock_12_out), .Q(out_77));  // open: clr
  Clock clock_12 (.out(clock_12_out));
  Register #(.width(32)) s1 (.D(r17in), .en(in_37), .clk(clock_13_out), .Q(out_81));  // open: clr
  Clock clock_13 (.out(clock_13_out));
  Register #(.width(32)) register_4 (.D(in_41), .en(in_45), .clk(clock_14_out), .Q(out_85));  // open: clr
  Clock clock_14 (.out(clock_14_out));
  Register #(.width(32)) t9_r24 (.D(in_49), .en(in_53), .clk(clock_15_out), .Q(out_89));  // open: clr
  Clock clock_15 (.out(clock_15_out));
  Register #(.width(32)) register_5 (.D(in_57), .en(in_61), .clk(clock_16_out), .Q(out_93));  // open: clr
  Clock clock_16 (.out(clock_16_out));
  Register #(.width(32)) r2 (.D(r2in), .en(r2we), .clk(clock_17_out), .Q(r2out));  // open: clr
  Clock clock_17 (.out(clock_17_out));
  Register #(.width(32)) r6 (.D(r6in), .en(r6we), .clk(clock_18_out), .Q(r6out));  // open: clr
  Clock clock_18 (.out(clock_18_out));
  Register #(.width(32)) t2 (.D(r10in), .en(in_22), .clk(clock_19_out), .Q(out_74));  // open: clr
  Clock clock_19 (.out(clock_19_out));
  Register #(.width(32)) register_6 (.D(r14in), .en(in_30), .clk(clock_20_out), .Q(out_78));  // open: clr
  Clock clock_20 (.out(clock_20_out));
  Register #(.width(32)) s2 (.D(in_34), .en(in_38), .clk(clock_21_out), .Q(out_82));  // open: clr
  Clock clock_21 (.out(clock_21_out));
  Register #(.width(32)) register_7 (.D(in_42), .en(in_46), .clk(clock_22_out), .Q(out_86));  // open: clr
  Clock clock_22 (.out(clock_22_out));
  Register #(.width(32)) register_8 (.D(in_50), .en(in_54), .clk(clock_23_out), .Q(out_90));  // open: clr
  Clock clock_23 (.out(clock_23_out));
  Register #(.width(32)) register_9 (.D(in_58), .en(in_62), .clk(clock_24_out), .Q(out_94));  // open: clr
  Clock clock_24 (.out(clock_24_out));
  Register #(.width(32)) r3 (.D(r3in), .en(r3we), .clk(clock_25_out), .Q(r3out));  // open: clr
  Clock clock_25 (.out(clock_25_out));
  Register #(.width(32)) r7 (.D(r7in), .en(r7we), .clk(clock_26_out), .Q(r7out));  // open: clr
  Clock clock_26 (.out(clock_26_out));
  Register #(.width(32)) t3 (.D(r11in), .en(in_23), .clk(clock_27_out), .Q(out_75));  // open: clr
  Clock clock_27 (.out(clock_27_out));
  Register #(.width(32)) register_10 (.D(r15in), .en(in_31), .clk(clock_28_out), .Q(out_79));  // open: clr
  Clock clock_28 (.out(clock_28_out));
  Register #(.width(32)) s3 (.D(in_35), .en(in_39), .clk(clock_29_out), .Q(out_83));  // open: clr
  Clock clock_29 (.out(clock_29_out));
  Register #(.width(32)) register_11 (.D(in_43), .en(in_47), .clk(clock_30_out), .Q(out_87));  // open: clr
  Clock clock_30 (.out(clock_30_out));
  Register #(.width(32)) register_12 (.D(in_51), .en(in_55), .clk(clock_31_out), .Q(out_91));  // open: clr
  Clock clock_31 (.out(clock_31_out));
  Register #(.width(32)) r31 (.D(r31in), .en(r31write), .clk(clock_32_out), .Q(r31out));  // open: clr
  Clock clock_32 (.out(clock_32_out));
endmodule

module ALU (
  input  [2:0] ALU_Signal,
  input  [31:0] IN1,
  input  [31:0] IN2,
  output [31:0] ALU_OUT
);

  wire comparator_1_eq, comparator_1_gt;
  wire [4:0] bit_extender_1_out;
  wire [31:0] adder_1_out, bit_extender_2_out, bit_extender_3_out, LO_q, multiplier_1_out, shifter_1_out,
       shifter_2_out, subtractor_1_out;

  Bit_Extender #(.in_width(32), .out_width(5), .\type ("zero")) bit_extender_1 (.in(IN2), .out(bit_extender_1_out));
  Adder #(.width(32)) adder_1 (.a(IN1), .b(IN2), .out(adder_1_out));  // open: cin, cout
  Subtractor #(.width(32)) subtractor_1 (.a(IN1), .b(IN2), .out(subtractor_1_out));  // open: bin, bout
  Multiplier #(.width(32)) multiplier_1 (.a(IN1), .b(IN2), .out(multiplier_1_out));  // open: cin, cout
  Comparator #(.width(32)) comparator_1 (.a(IN1), .b(IN2), .gt(comparator_1_gt), .eq(comparator_1_eq));  // open: lt
  Shifter #(.width(32)) shifter_1 (.in(IN1), .\dist (bit_extender_1_out), .out(shifter_1_out));
  Shifter #(.shift("lr"), .width(32)) shifter_2 (.in(IN1), .\dist (bit_extender_1_out), .out(shifter_2_out));
  assign bit_extender_2_out = {{31{1'b0}}, comparator_1_gt};  // Bit_Extender bit_extender_2
  Multiplexer #(.enable("false"), .select(3), .width(32)) multiplexer_1 (
    .in0(adder_1_out), .in1(subtractor_1_out), .in2(multiplier_1_out), .in3(shifter_1_out),
    .in4(shifter_2_out), .in5(bit_extender_2_out), .in6(bit_extender_3_out), .in7(LO_q), .out(ALU_OUT),
    .sel(ALU_Signal));
  assign bit_extender_3_out = {{31{1'b0}}, comparator_1_eq};  // Bit_Extender bit_extender_3
  Register #(.width(32)) HI ();  // open: D, en, clk, Q, clr
  Register #(.width(32)) LO (.D(multiplier_1_out), .en(1'b1), .clk(1'b1), .Q(LO_q), .clr(1'b0));
endmodule

module DataMem (
  input  [15:0] readaddress,
  input  Mem_Signal,
  input  [31:0] writedata,
  output [31:0] DataOut
);

  wire clock_1_out;

  Clock clock_1 (.out(clock_1_out));
  RAM #(.addrWidth(16), .dataWidth(32)) ram_1 (
    .addr(readaddress), .we(Mem_Signal), .oe(1'b1), .clk(clock_1_out), .din(writedata), .dout(DataOut));
endmodule

module InsMem (
  input  [15:0] in_1,
  output [31:0] out_2
);

  ROM #(.addrWidth(16), .dataWidth(32)) rom_1 (.addr(in_1), .data(out_2));

  // Notes on the sheet:
  //   contents of rom_1 (hex, n*v repeats v):
  //   21000000 8c08ff00 1100000b 8c10ff01 9c00ff00 21000077 12080031 21000073 12080031 21000061 12080031
  //   21000064 12080031 21330000 21540000 2719820 292a020 8c0bff10 11600001 9c09ff11 9c0aff12 23200000
  //   9c19ff13 21800001 9c0cff10 21000001 8c0bff10 11600001 9c13ff11 9c14ff12 232000ff 9c19ff13 9c0cff10
  //   21000080 1268000f 23200100 21000001 260482a 11280008 333502a 11480006 280582a 11680004 334602a
  //   11880002 8000000 2100ffff 9c08ff13 800003f 21000080 12880002 8000023 2100ffff 9c08ff13 800003f
  //   2252ffff 8000001 22520001 8000001 2231ffff 8000001 22310001 8000001
endmodule

module PC (
  input  [15:0] in_1,
  output [15:0] out_2
);

  wire clock_1_out;

  Clock clock_1 (.out(clock_1_out));
  Register #(.width(16)) register_1 (.D(in_1), .en(1'b1), .clk(clock_1_out), .Q(out_2));  // open: clr
endmodule

module Control (
  input  [31:0] Instruction,
  output beq,
  output jalsignal,
  output bne,
  output [1:0] PCsrc,
  output MemtoReg,
  output we_reg,
  output [2:0] ALU_Signal,
  output RegtoMem,
  output [1:0] toALU_Signal,
  output [4:0] sa,
  output [4:0] ins16_20,
  output [4:0] ins11_15,
  output [4:0] ins21_25,
  output [15:0] Imm0_15
);

  wire and_4_out, and_5_out, and_6_out, and_7_out, and_8_out, and_9_out, and_10_out, and_11_out, and_12_out,
       and_13_out, and_14_out, and_16_out, and_17_out, and_18_out, and_19_out, and_20_out, nor_2_out,
       not_1_out, not_2_out, not_3_out, not_4_out, not_5_out, not_6_out, not_7_out, not_8_out, not_9_out,
       not_10_out, not_11_out, not_12_out, not_13_out, not_14_out, or_1_out, or_2_out, or_3_out, or_5_out,
       or_6_out, or_7_out, or_8_out;
  wire [4:0] multiplexer_1_out, multiplexer_2_out, multiplexer_4_out;

  and and_1 (jalsignal, Instruction[26], Instruction[27], not_1_out);
  not not_1 (not_1_out, Instruction[31]);
  and and_2 (MemtoReg, Instruction[27], not_2_out, Instruction[31]);
  not not_2 (not_2_out, Instruction[28]);
  and and_3 (RegtoMem, Instruction[28], Instruction[31]);
  or or_1 (or_1_out, Instruction[2], Instruction[0], Instruction[1], Instruction[3], Instruction[4], Instruction[5]);
  and and_4 (and_4_out, Instruction[3], Instruction[4]);
  and and_5 (and_5_out, and_4_out, not_3_out);
  or or_2 (or_2_out, Instruction[26], Instruction[27], Instruction[28], Instruction[30], Instruction[31], Instruction[29]);
  not not_3 (not_3_out, or_2_out);
  not not_4 (not_4_out, Instruction[5]);
  and and_6 (and_6_out, Instruction[27], not_5_out);
  not not_5 (not_5_out, Instruction[26]);
  and and_7 (and_7_out, Instruction[3], Instruction[4]);
  and and_8 (and_8_out, Instruction[26], Instruction[27], Instruction[31]);
  nor nor_1 (we_reg, and_6_out, Instruction[28], and_5_out);
  and and_9 (and_9_out, Instruction[0], Instruction[4]);
  and and_10 (and_10_out, Instruction[1], not_4_out);
  and and_11 (and_11_out, Instruction[1], Instruction[3], Instruction[5]);
  or or_3 (or_3_out, Instruction[29], Instruction[30]);
  or or_4 (toALU_Signal[0], Instruction[29], Instruction[30], Instruction[31]);
  or or_5 (or_5_out, and_9_out, and_10_out, and_11_out);
  Multiplexer #(.enable("false"), .width(5)) multiplexer_1 (
    .in0(Instruction[15:11]), .in1({5{1'b1}}), .out(multiplexer_1_out), .sel(jalsignal));
  not not_6 (not_6_out, or_1_out);
  and and_12 (and_12_out, Instruction[1], Instruction[5]);
  Multiplexer #(.enable("false"), .width(5)) multiplexer_2 (
    .in0(multiplexer_1_out), .in1(Instruction[25:21]), .out(multiplexer_2_out), .sel(or_3_out));
  or or_6 (or_6_out, and_9_out, not_6_out, and_7_out);
  or or_7 (or_7_out, and_12_out, and_9_out, not_6_out);
  Multiplexer #(.enable("false"), .width(5)) multiplexer_3 (
    .in0(multiplexer_2_out), .in1(Instruction[20:16]), .out(ins11_15), .sel(and_8_out));
  not not_7 (not_7_out, or_3_out);
  not not_8 (not_8_out, Instruction[27]);
  and and_13 (and_13_out, not_8_out, Instruction[28]);
  not not_9 (not_9_out, or_8_out);
  or or_8 (or_8_out, Instruction[26], Instruction[27], Instruction[28], Instruction[30], Instruction[31], Instruction[29]);
  not not_10 (not_10_out, Instruction[27]);
  and and_14 (and_14_out, Instruction[28], not_10_out);
  not not_11 (not_11_out, Instruction[4]);
  not not_12 (not_12_out, Instruction[5]);
  and and_15 (ALU_Signal[0], not_7_out, not_9_out, or_7_out);
  and and_16 (and_16_out, not_7_out, not_9_out, or_6_out);
  and and_17 (and_17_out, not_7_out, not_9_out, or_5_out);
  Multiplexer #(.enable("false"), .width(5)) multiplexer_4 (
    .in0(Instruction[25:21]), .in1(multiplexer_1_out), .out(multiplexer_4_out), .sel(or_3_out));
  and and_18 (and_18_out, Instruction[3], not_11_out, not_12_out);
  or or_9 (ALU_Signal[1], and_13_out, and_16_out);
  or or_10 (ALU_Signal[2], and_13_out, and_17_out);
  nor nor_2 (nor_2_out, Instruction[4], Instruction[5]);
  and and_19 (and_19_out, and_18_out, not_9_out);
  not not_13 (not_13_out, Instruction[31]);
  and and_20 (and_20_out, not_13_out, Instruction[27]);
  and and_21 (toALU_Signal[1], not_9_out, nor_2_out);
  or or_11 (PCsrc[0], and_14_out, and_19_out);
  or or_12 (PCsrc[1], and_19_out, and_20_out);
  Multiplexer #(.enable("false"), .width(5)) multiplexer_5 (
    .in0(multiplexer_4_out), .in1({5{1'b1}}), .out(ins21_25), .sel(and_19_out));
  not not_14 (not_14_out, Instruction[26]);
  and and_22 (beq, not_14_out, PCsrc[0]);
  and and_23 (bne, Instruction[26], PCsrc[0]);

  assign Imm0_15 = Instruction[15:0];
  assign ins16_20 = Instruction[20:16];
  assign sa = Instruction[10:6];
endmodule

module RegisterFile (
  input  we_reg,
  input  [4:0] rsselect,
  input  [4:0] reg_towrite,
  input  [4:0] rtselect,
  input  [31:0] write_data,
  output [31:0] rs_data,
  output [31:0] rt_data
);

  wire demultiplexer_1_out1, demultiplexer_1_out2, demultiplexer_1_out3, demultiplexer_1_out4,
       demultiplexer_1_out5, demultiplexer_1_out6, demultiplexer_1_out7, demultiplexer_1_out8,
       demultiplexer_1_out9, demultiplexer_1_out10, demultiplexer_1_out11, demultiplexer_1_out12,
       demultiplexer_1_out13, demultiplexer_1_out14, demultiplexer_1_out15, demultiplexer_1_out16,
       demultiplexer_1_out17, demultiplexer_1_out18, demultiplexer_1_out19, demultiplexer_1_out20,
       demultiplexer_1_out21, demultiplexer_1_out22, demultiplexer_1_out23, demultiplexer_1_out24,
       demultiplexer_1_out25, demultiplexer_1_out26, demultiplexer_1_out27, demultiplexer_1_out28,
       demultiplexer_1_out29, demultiplexer_1_out30, demultiplexer_1_out31;
  wire [31:0] demultiplexer_2_out0, demultiplexer_2_out1, demultiplexer_2_out2, demultiplexer_2_out3,
       demultiplexer_2_out4, demultiplexer_2_out5, demultiplexer_2_out6, demultiplexer_2_out7,
       demultiplexer_2_out8, demultiplexer_2_out9, demultiplexer_2_out10, demultiplexer_2_out11,
       demultiplexer_2_out12, demultiplexer_2_out13, demultiplexer_2_out14, demultiplexer_2_out15,
       demultiplexer_2_out16, demultiplexer_2_out17, demultiplexer_2_out18, demultiplexer_2_out19,
       demultiplexer_2_out20, demultiplexer_2_out21, demultiplexer_2_out22, demultiplexer_2_out23,
       demultiplexer_2_out24, demultiplexer_2_out25, demultiplexer_2_out26, demultiplexer_2_out27,
       demultiplexer_2_out28, demultiplexer_2_out29, demultiplexer_2_out30, demultiplexer_2_out31,
       registers_1_out_72, registers_1_out_73, registers_1_out_74, registers_1_out_75, registers_1_out_76,
       registers_1_out_77, registers_1_out_78, registers_1_out_79, registers_1_out_80, registers_1_out_81,
       registers_1_out_82, registers_1_out_83, registers_1_out_84, registers_1_out_85, registers_1_out_86,
       registers_1_out_87, registers_1_out_88, registers_1_out_89, registers_1_out_90, registers_1_out_91,
       registers_1_out_92, registers_1_out_93, registers_1_out_94, registers_1_r0out, registers_1_r1out,
       registers_1_r2out, registers_1_r3out, registers_1_r4out, registers_1_r5out, registers_1_r6out,
       registers_1_r7out, registers_1_r31out;

  Demultiplexer #(.enable("false"), .select(5)) demultiplexer_1 (
    .out1(demultiplexer_1_out1), .out2(demultiplexer_1_out2), .out3(demultiplexer_1_out3),
    .out4(demultiplexer_1_out4), .out5(demultiplexer_1_out5), .out6(demultiplexer_1_out6),
    .out7(demultiplexer_1_out7), .out8(demultiplexer_1_out8), .out9(demultiplexer_1_out9),
    .out10(demultiplexer_1_out10), .out11(demultiplexer_1_out11), .out12(demultiplexer_1_out12),
    .out13(demultiplexer_1_out13), .out14(demultiplexer_1_out14), .out15(demultiplexer_1_out15),
    .out16(demultiplexer_1_out16), .out17(demultiplexer_1_out17), .out18(demultiplexer_1_out18),
    .out19(demultiplexer_1_out19), .out20(demultiplexer_1_out20), .out21(demultiplexer_1_out21),
    .out22(demultiplexer_1_out22), .out23(demultiplexer_1_out23), .out24(demultiplexer_1_out24),
    .out25(demultiplexer_1_out25), .out26(demultiplexer_1_out26), .out27(demultiplexer_1_out27),
    .out28(demultiplexer_1_out28), .out29(demultiplexer_1_out29), .out30(demultiplexer_1_out30),
    .out31(demultiplexer_1_out31), .in(we_reg), .sel(reg_towrite));  // open: out0
  Demultiplexer #(.enable("false"), .select(5), .width(32)) demultiplexer_2 (
    .out0(demultiplexer_2_out0), .out1(demultiplexer_2_out1), .out2(demultiplexer_2_out2),
    .out3(demultiplexer_2_out3), .out4(demultiplexer_2_out4), .out5(demultiplexer_2_out5),
    .out6(demultiplexer_2_out6), .out7(demultiplexer_2_out7), .out8(demultiplexer_2_out8),
    .out9(demultiplexer_2_out9), .out10(demultiplexer_2_out10), .out11(demultiplexer_2_out11),
    .out12(demultiplexer_2_out12), .out13(demultiplexer_2_out13), .out14(demultiplexer_2_out14),
    .out15(demultiplexer_2_out15), .out16(demultiplexer_2_out16), .out17(demultiplexer_2_out17),
    .out18(demultiplexer_2_out18), .out19(demultiplexer_2_out19), .out20(demultiplexer_2_out20),
    .out21(demultiplexer_2_out21), .out22(demultiplexer_2_out22), .out23(demultiplexer_2_out23),
    .out24(demultiplexer_2_out24), .out25(demultiplexer_2_out25), .out26(demultiplexer_2_out26),
    .out27(demultiplexer_2_out27), .out28(demultiplexer_2_out28), .out29(demultiplexer_2_out29),
    .out30(demultiplexer_2_out30), .out31(demultiplexer_2_out31), .in(write_data), .sel(reg_towrite));
  registers registers_1 (
    .r0in(demultiplexer_2_out0), .r1in(demultiplexer_2_out1), .r2in(demultiplexer_2_out2),
    .r3in(demultiplexer_2_out3), .r1we(demultiplexer_1_out1), .r2we(demultiplexer_1_out2),
    .r3we(demultiplexer_1_out3), .r4in(demultiplexer_2_out4), .r5in(demultiplexer_2_out5),
    .r6in(demultiplexer_2_out6), .r7in(demultiplexer_2_out7), .r4we(demultiplexer_1_out4),
    .r5we(demultiplexer_1_out5), .r6we(demultiplexer_1_out6), .r7we(demultiplexer_1_out7),
    .r8in(demultiplexer_2_out8), .r9in(demultiplexer_2_out9), .r10in(demultiplexer_2_out10),
    .r11in(demultiplexer_2_out11), .r8we(demultiplexer_1_out8), .in_21(demultiplexer_1_out9),
    .in_22(demultiplexer_1_out10), .in_23(demultiplexer_1_out11), .r12in(demultiplexer_2_out12),
    .r13in(demultiplexer_2_out13), .r14in(demultiplexer_2_out14), .r15in(demultiplexer_2_out15),
    .in_28(demultiplexer_1_out12), .in_29(demultiplexer_1_out13), .in_30(demultiplexer_1_out14),
    .in_31(demultiplexer_1_out15), .r16in(demultiplexer_2_out16), .r17in(demultiplexer_2_out17),
    .in_34(demultiplexer_2_out18), .in_35(demultiplexer_2_out19), .in_36(demultiplexer_1_out16),
    .in_37(demultiplexer_1_out17), .in_38(demultiplexer_1_out18), .in_39(demultiplexer_1_out19),
    .in_40(demultiplexer_2_out20), .in_41(demultiplexer_2_out21), .in_42(demultiplexer_2_out22),
    .in_43(demultiplexer_2_out23), .in_44(demultiplexer_1_out20), .in_45(demultiplexer_1_out21),
    .in_46(demultiplexer_1_out22), .in_47(demultiplexer_1_out23), .in_48(demultiplexer_2_out24),
    .in_49(demultiplexer_2_out25), .in_50(demultiplexer_2_out26), .in_51(demultiplexer_2_out27),
    .in_52(demultiplexer_1_out24), .in_53(demultiplexer_1_out25), .in_54(demultiplexer_1_out26),
    .in_55(demultiplexer_1_out27), .in_56(demultiplexer_2_out28), .in_57(demultiplexer_2_out29),
    .in_58(demultiplexer_2_out30), .r31in(demultiplexer_2_out31), .in_60(demultiplexer_1_out28),
    .in_61(demultiplexer_1_out29), .in_62(demultiplexer_1_out30), .r31write(demultiplexer_1_out31),
    .r0out(registers_1_r0out), .r1out(registers_1_r1out), .r2out(registers_1_r2out),
    .r3out(registers_1_r3out), .r4out(registers_1_r4out), .r5out(registers_1_r5out),
    .r6out(registers_1_r6out), .r7out(registers_1_r7out), .out_72(registers_1_out_72),
    .out_73(registers_1_out_73), .out_74(registers_1_out_74), .out_75(registers_1_out_75),
    .out_76(registers_1_out_76), .out_77(registers_1_out_77), .out_78(registers_1_out_78),
    .out_79(registers_1_out_79), .out_80(registers_1_out_80), .out_81(registers_1_out_81),
    .out_82(registers_1_out_82), .out_83(registers_1_out_83), .out_84(registers_1_out_84),
    .out_85(registers_1_out_85), .out_86(registers_1_out_86), .out_87(registers_1_out_87),
    .out_88(registers_1_out_88), .out_89(registers_1_out_89), .out_90(registers_1_out_90),
    .out_91(registers_1_out_91), .out_92(registers_1_out_92), .out_93(registers_1_out_93),
    .out_94(registers_1_out_94), .r31out(registers_1_r31out));
  Multiplexer #(.enable("false"), .select(5), .width(32)) multiplexer_1 (
    .in0(registers_1_r0out), .in1(registers_1_r1out), .in2(registers_1_r2out), .in3(registers_1_r3out),
    .in4(registers_1_r4out), .in5(registers_1_r5out), .in6(registers_1_r6out), .in7(registers_1_r7out),
    .in8(registers_1_out_72), .in9(registers_1_out_73), .in10(registers_1_out_74), .in11(registers_1_out_75),
    .in12(registers_1_out_76), .in13(registers_1_out_77), .in14(registers_1_out_78),
    .in15(registers_1_out_79), .in16(registers_1_out_80), .in17(registers_1_out_81),
    .in18(registers_1_out_82), .in19(registers_1_out_83), .in20(registers_1_out_84),
    .in21(registers_1_out_85), .in22(registers_1_out_86), .in23(registers_1_out_87),
    .in24(registers_1_out_88), .in25(registers_1_out_89), .in26(registers_1_out_90),
    .in27(registers_1_out_91), .in28(registers_1_out_92), .in29(registers_1_out_93),
    .in30(registers_1_out_94), .in31(registers_1_r31out), .out(rs_data), .sel(rsselect));
  Multiplexer #(.enable("false"), .select(5), .width(32)) multiplexer_2 (
    .in0(registers_1_r0out), .in1(registers_1_r1out), .in2(registers_1_r2out), .in3(registers_1_r3out),
    .in4(registers_1_r4out), .in5(registers_1_r5out), .in6(registers_1_r6out), .in7(registers_1_r7out),
    .in8(registers_1_out_72), .in9(registers_1_out_73), .in10(registers_1_out_74), .in11(registers_1_out_75),
    .in12(registers_1_out_76), .in13(registers_1_out_77), .in14(registers_1_out_78),
    .in15(registers_1_out_79), .in16(registers_1_out_80), .in17(registers_1_out_81),
    .in18(registers_1_out_82), .in19(registers_1_out_83), .in20(registers_1_out_84),
    .in21(registers_1_out_85), .in22(registers_1_out_86), .in23(registers_1_out_87),
    .in24(registers_1_out_88), .in25(registers_1_out_89), .in26(registers_1_out_90),
    .in27(registers_1_out_91), .in28(registers_1_out_92), .in29(registers_1_out_93),
    .in30(registers_1_out_94), .in31(registers_1_r31out), .out(rt_data), .sel(rtselect));
endmodule

module NewMain (
);

  wire clock_1_out, clock_2_out, keyboard_1_avail, newbus_1_readwrite_lwsw,
       newkbcontroller_1_databuswriteenable, newkbcontroller_1_keyboardre, newmem_1_databuswrite,
       processor_1_addrbuswrite, processor_1_controlbuswrite, processor_1_databuswrite,
       processor_1_memwriteenable, videocontroller_1_databuswriteenable, videocontroller_1_resetsignal,
       videocontroller_1_wergb;
  wire [6:0] keyboard_1_data;
  wire [7:0] videocontroller_1_xcoord, videocontroller_1_ycoord;
  wire [15:0] newbus_1_addrfrombus, processor_1_addr;
  wire [23:0] videocontroller_1_colordata;
  wire [31:0] newbus_1_datafrombus, newkbcontroller_1_datatobus, newmem_1_datatobus, processor_1_data,
       videocontroller_1_datatobus;

  Processor processor_1 (
    .Addr(processor_1_addr), .MemWriteEnable(processor_1_memwriteenable), .Data(processor_1_data),
    .AddrBusWrite(processor_1_addrbuswrite), .DatabusWrite(processor_1_databuswrite),
    .ControlBusWrite(processor_1_controlbuswrite), .DataFromBus(newbus_1_datafrombus));
  NewMem newmem_1 (
    .MemWriteEnable(newbus_1_readwrite_lwsw), .DataFromBus(newbus_1_datafrombus),
    .AddressFromBus(newbus_1_addrfrombus), .DataToBus(newmem_1_datatobus),
    .DataBusWrite(newmem_1_databuswrite));
  Clock clock_1 (.out(clock_1_out));
  NewKBController newkbcontroller_1 (
    .DataToBus(newkbcontroller_1_datatobus), .DataBusWriteEnable(newkbcontroller_1_databuswriteenable),
    .KeyboardRE(newkbcontroller_1_keyboardre), .AddrFBus(newbus_1_addrfrombus), .WE(newbus_1_readwrite_lwsw),
    .Available(keyboard_1_avail), .DataFromBus(newbus_1_datafrombus), .KeyBoardData(keyboard_1_data));
  // Probe on keyboard_1_data
  // Probe on videocontroller_1_xcoord
  // Probe on videocontroller_1_ycoord
  // Probe on videocontroller_1_colordata
  Clock clock_2 (.out(clock_2_out));
  VideoController videocontroller_1 (
    .WERGB(videocontroller_1_wergb), .DataToBus(videocontroller_1_datatobus),
    .DataBusWriteEnable(videocontroller_1_databuswriteenable), .xcoord(videocontroller_1_xcoord),
    .ycoord(videocontroller_1_ycoord), .colordata(videocontroller_1_colordata),
    .resetSignal(videocontroller_1_resetsignal), .AddrFBus(newbus_1_addrfrombus),
    .DataFromBus(newbus_1_datafrombus), .WE(newbus_1_readwrite_lwsw));
  Newbus newbus_1 (
    .AddrFromBus(newbus_1_addrfrombus), .DataFromBus(newbus_1_datafrombus),
    .readwrite_lwsw(newbus_1_readwrite_lwsw), .AddrFromProc(processor_1_addr),
    .AddrBusWriteProc(processor_1_addrbuswrite), .DataFromProc(processor_1_data),
    .MemWriteEnable(processor_1_memwriteenable), .CtrlBusWrite(processor_1_controlbuswrite),
    .writeProc(processor_1_databuswrite), .writeMem(newmem_1_databuswrite),
    .DataFromKBController(newkbcontroller_1_datatobus), .writeKBC(newkbcontroller_1_databuswriteenable),
    .DataFromMem(newmem_1_datatobus), .DataFromVideoControl(videocontroller_1_datatobus),
    .writeVC(videocontroller_1_databuswriteenable));
  Keyboard keyboard_1 (
    .clk(clock_1_out), .re(newkbcontroller_1_keyboardre), .avail(keyboard_1_avail), .data(keyboard_1_data));  // open: clr
  // RGB_Video #(.height(256), .scale(4), .width(256)) rgb_video_1: pin names not known; wires that end beside it: videocontroller_1_resetsignal, clock_2_out, videocontroller_1_wergb, videocontroller_1_xcoord, videocontroller_1_ycoord, videocontroller_1_colordata
endmodule

module Newbus (
  input  [15:0] AddrFromProc,
  input  AddrBusWriteProc,
  input  [31:0] DataFromProc,
  input  writeProc,
  input  MemWriteEnable,
  input  CtrlBusWrite,
  input  [31:0] DataFromMem,
  input  writeMem,
  input  [31:0] DataFromKBController,
  input  writeKBC,
  input  [31:0] DataFromVideoControl,
  input  writeVC,
  output [15:0] AddrFromBus,
  output [31:0] DataFromBus,
  output readwrite_lwsw
);

  assign AddrFromBus = AddrBusWriteProc ? AddrFromProc : 16'bz;  // Controlled_Buffer controlled_buffer_1
  assign DataFromBus = writeProc ? DataFromProc : 32'bz;  // Controlled_Buffer controlled_buffer_2
  assign readwrite_lwsw = CtrlBusWrite ? MemWriteEnable : 1'bz;  // Controlled_Buffer controlled_buffer_3
  assign DataFromBus = writeMem ? DataFromMem : 32'bz;  // Controlled_Buffer controlled_buffer_4
  assign DataFromBus = writeKBC ? DataFromKBController : 32'bz;  // Controlled_Buffer controlled_buffer_5
  assign DataFromBus = writeVC ? DataFromVideoControl : 32'bz;  // Controlled_Buffer controlled_buffer_6
  // Probe on DataFromBus
endmodule

module NewMem (
  input  MemWriteEnable,
  input  [31:0] DataFromBus,
  input  [15:0] AddressFromBus,
  output [31:0] DataToBus,
  output DataBusWrite
);

  wire clock_1_out, comparator_1_lt, comparator_2_eq, controlled_buffer_2_out;
  wire [15:0] controlled_buffer_1_out;

  Comparator #(.mode("unsigned"), .width(16)) comparator_1 (
    .a(AddressFromBus), .b(16'hff00), .lt(comparator_1_lt));  // open: gt, eq
  assign controlled_buffer_1_out = comparator_1_lt ? AddressFromBus : 16'bz;  // Controlled_Buffer controlled_buffer_1
  Comparator #(.width(1)) comparator_2 (.a(MemWriteEnable), .b(1'b1), .eq(comparator_2_eq));  // open: gt, lt
  assign controlled_buffer_2_out = comparator_1_lt ? MemWriteEnable : 1'bz;  // Controlled_Buffer controlled_buffer_2
  and and_1 (DataBusWrite, comparator_2_eq, comparator_1_lt);
  Clock clock_1 (.out(clock_1_out));
  RAM #(.addrWidth(16), .dataWidth(32)) ram_1 (
    .addr(controlled_buffer_1_out), .we(controlled_buffer_2_out), .oe(1'b1), .clk(clock_1_out),
    .din(DataFromBus), .dout(DataToBus));
endmodule

module NewKBController (
  input  Available,
  input  [31:0] DataFromBus,
  input  WE,
  input  [15:0] AddrFBus,
  input  [6:0] KeyBoardData,
  output KeyboardRE,
  output DataBusWriteEnable,
  output [31:0] DataToBus
);

  wire and_1_out, and_2_out, and_3_out, and_4_out, and_5_out, bit_extender_1_out, clock_1_out, clock_2_out,
       comparator_1_eq, controlled_buffer_1_out, lwStatusReg_out, not_1_out, not_2_out, not_3_out, not_4_out,
       not_5_out, not_6_out, or_1_out, Status_q, swStatusReg_out;
  wire [6:0] data_q;
  wire [31:0] bit_extender_2_out, bit_extender_3_out;

  not not_1 (not_1_out, AddrFBus[1]);
  Comparator #(.width(14)) comparator_1 (.a(AddrFBus[15:2]), .b(14'h3fc0), .eq(comparator_1_eq));  // open: gt, lt
  and swStatusReg (swStatusReg_out, WE, and_3_out);
  not not_2 (not_2_out, AddrFBus[0]);
  and and_1 (and_1_out, not_2_out, not_3_out);
  not not_3 (not_3_out, AddrFBus[1]);
  and and_2 (and_2_out, AddrFBus[0], not_1_out);
  assign controlled_buffer_1_out = not_4_out ? Available : 1'bz;  // Controlled_Buffer controlled_buffer_1
  not not_4 (not_4_out, swStatusReg_out);
  Bit_Extender #(.in_width(32), .out_width(1), .\type ("zero")) bit_extender_1 (
    .in(DataFromBus), .out(bit_extender_1_out));
  and and_3 (and_3_out, and_1_out, comparator_1_eq);
  assign controlled_buffer_1_out = swStatusReg_out ? bit_extender_1_out : 1'bz;  // Controlled_Buffer controlled_buffer_2
  or or_1 (or_1_out, controlled_buffer_1_out, swStatusReg_out);
  not not_5 (not_5_out, Status_q);
  Register #(.width(1)) Status (
    .D(controlled_buffer_1_out), .en(or_1_out), .clk(clock_1_out), .Q(Status_q));  // open: clr
  Clock clock_1 (.out(clock_1_out));
  not not_6 (not_6_out, swStatusReg_out);
  // Probe on data_q
  Register #(.width(7)) data (.D(KeyBoardData), .en(not_5_out), .clk(clock_2_out), .Q(data_q));  // open: clr
  Clock clock_2 (.out(clock_2_out));
  assign bit_extender_2_out = {{31{1'b0}}, Status_q};  // Bit_Extender bit_extender_2
  assign bit_extender_3_out = {{25{1'b0}}, data_q};  // Bit_Extender bit_extender_3
  and and_4 (and_4_out, and_2_out, comparator_1_eq);
  not not_7 (KeyboardRE, Status_q);
  assign DataToBus = and_3_out ? bit_extender_2_out : 32'bz;  // Controlled_Buffer controlled_buffer_3
  and lwStatusReg (lwStatusReg_out, not_6_out, and_3_out);
  and and_5 (and_5_out, Status_q, and_4_out);
  assign DataToBus = and_4_out ? bit_extender_3_out : 32'bz;  // Controlled_Buffer controlled_buffer_4
  or or_2 (DataBusWriteEnable, lwStatusReg_out, and_5_out);
endmodule

module VideoController (
  input  WE,
  input  [31:0] DataFromBus,
  input  [15:0] AddrFBus,
  output [31:0] DataToBus,
  output DataBusWriteEnable,
  output WERGB,
  output [7:0] xcoord,
  output [7:0] ycoord,
  output [23:0] colordata,
  output resetSignal
);

  wire and_1_out, and_2_out, and_3_out, and_4_out, and_5_out, and_6_out, and_7_out, and_8_out, and_9_out,
       and_10_out, and_11_out, bit_extender_1_out, clock_1_out, multiplexer_1_out, nor_1_out, not_1_out,
       not_2_out, not_3_out, not_4_out, or_1_out;
  wire [7:0] bit_extender_2_out, bit_extender_3_out;
  wire [23:0] bit_extender_4_out;
  wire [31:0] controlled_buffer_1_out, controlled_buffer_2_out, controlled_buffer_3_out,
       controlled_buffer_4_out;

  and and_1 (and_1_out, AddrFBus[8], AddrFBus[9], AddrFBus[10], AddrFBus[11], AddrFBus[13], AddrFBus[14], AddrFBus[15], AddrFBus[12]);
  not not_1 (not_1_out, WERGB);
  not not_2 (not_2_out, AddrFBus[1]);
  and and_2 (and_2_out, AddrFBus[0], not_2_out, AddrFBus[4]);
  not not_3 (not_3_out, AddrFBus[0]);
  and and_3 (and_3_out, AddrFBus[1], not_3_out, AddrFBus[4]);
  and and_4 (and_4_out, AddrFBus[0], AddrFBus[1], AddrFBus[4], and_1_out);
  assign controlled_buffer_1_out = and_5_out ? DataFromBus : 32'bz;  // Controlled_Buffer controlled_buffer_1
  and and_5 (and_5_out, nor_1_out, AddrFBus[4], and_1_out);
  nor nor_1 (nor_1_out, AddrFBus[0], AddrFBus[1]);
  assign controlled_buffer_2_out = and_6_out ? DataFromBus : 32'bz;  // Controlled_Buffer controlled_buffer_2
  and and_6 (and_6_out, and_3_out, and_1_out);
  assign controlled_buffer_3_out = and_4_out ? DataFromBus : 32'bz;  // Controlled_Buffer controlled_buffer_3
  Bit_Extender #(.in_width(32), .out_width(1), .\type ("zero")) bit_extender_1 (
    .in(controlled_buffer_1_out), .out(bit_extender_1_out));
  Multiplexer #(.enable("false")) multiplexer_1 (
    .in0(bit_extender_1_out), .in1(not_1_out), .out(multiplexer_1_out), .sel(WERGB));
  assign controlled_buffer_4_out = and_7_out ? DataFromBus : 32'bz;  // Controlled_Buffer controlled_buffer_4
  and and_7 (and_7_out, and_2_out, and_1_out);
  and and_8 (and_8_out, WE, and_5_out);
  and and_9 (and_9_out, WE, and_7_out);
  and and_10 (and_10_out, WE, and_6_out);
  and and_11 (and_11_out, WE, and_4_out);
  Clock clock_1 (.out(clock_1_out));
  or or_1 (or_1_out, WERGB, and_8_out);
  Register xcoordinate (.D(bit_extender_2_out), .en(and_9_out), .clk(clock_1_out), .Q(xcoord));  // open: clr
  Bit_Extender #(.in_width(32), .out_width(8), .\type ("zero")) bit_extender_2 (
    .in(controlled_buffer_4_out), .out(bit_extender_2_out));
  Register ycoordinate (.D(bit_extender_3_out), .en(and_10_out), .clk(clock_1_out), .Q(ycoord));  // open: clr
  Bit_Extender #(.in_width(32), .out_width(8), .\type ("zero")) bit_extender_3 (
    .in(controlled_buffer_2_out), .out(bit_extender_3_out));
  Register #(.width(24)) color (
    .D(bit_extender_4_out), .en(and_11_out), .clk(clock_1_out), .Q(colordata));  // open: clr
  Bit_Extender #(.in_width(32), .out_width(24), .\type ("zero")) bit_extender_4 (
    .in(controlled_buffer_3_out), .out(bit_extender_4_out));
  Register #(.width(1)) register_1 (.D(multiplexer_1_out), .en(or_1_out), .clk(clock_1_out), .Q(WERGB));  // open: clr
  Comparator #(.width(24)) comparator_1 (.a(colordata), .b({24{1'b1}}), .eq(resetSignal));  // open: gt, lt
  not not_4 (not_4_out, WE);
  assign DataToBus = {{31{1'b0}}, WERGB};  // Bit_Extender bit_extender_5
  and and_12 (DataBusWriteEnable, not_4_out, and_5_out);
endmodule

module test (
  input  in_1,
  input  in_2,
  input  in_3,
  input  in_4,
  input  in_5,
  input  [7:0] in_6,
  input  [7:0] in_7,
  input  [23:0] in_8
);

  wire undriven;
  wire [6:0] keyboard_1_data;

  Keyboard keyboard_1 (.clk(undriven), .re(in_1), .clr(in_2), .data(keyboard_1_data));  // open: avail
  // Probe on keyboard_1_data
  // RGB_Video #(.height(256), .width(256)) rgb_video_1: pin names not known; wires that end beside it: in_3, in_4, in_5, in_6, in_7, in_8
endmodule
